// Logisim project Assignment 10.circ as structural Verilog: 5 circuits, main circuit main
module main (
  input  [3:0] A,
  input  [3:0] B,
  input  in_3,
  output out_4,
  output out_5,
  output out_6,
  output out_7,
  output Sum_difference
);

  wire n1_bit_adder_1_out_5, n1_bit_adder_2_out_5, n1_bit_adder_3_out_5, n1_bit_adder_4_out_5,
       n7_segment_display_1_a_2, n7_segment_display_1_b_2, n7_segment_display_1_c_2,
       n7_segment_display_1_d_2, n7_segment_display_1_e_2, n7_segment_display_1_f, n7_segment_display_1_g,
       n7_segment_display_4_a_2, n7_segment_display_4_b_2, n7_segment_display_4_c_2,
       n7_segment_display_4_d_2, n7_segment_display_4_e_2, n7_segment_display_4_f, n7_segment_display_4_g,
       xor_1_out, xor_2_out, xor_3_out, xor_4_out;

  xor xor_1 (xor_1_out, in_3, B[0]);
  _1_bit_adder u_1_bit_adder_1 (
    .in_1(A[0]), .in_2(xor_1_out), .in_3(in_3), .out_4(Sum_difference), .out_5(n1_bit_adder_1_out_5));
  _7_segment_display u_7_segment_display_1 (
    .A(Sum_difference), .B(out_7), .C(out_6), .D(out_5), .E(out_4), .a_2(n7_segment_display_1_a_2),
    .b_2(n7_segment_display_1_b_2), .c_2(n7_segment_display_1_c_2), .d_2(n7_segment_display_1_d_2),
    .e_2(n7_segment_display_1_e_2), .f(n7_segment_display_1_f), .g(n7_segment_display_1_g));
  xor xor_2 (xor_2_out, in_3, B[1]);
  _1_bit_adder u_1_bit_adder_2 (
    .in_1(A[1]), .in_2(xor_2_out), .in_3(n1_bit_adder_1_out_5), .out_4(out_7), .out_5(n1_bit_adder_2_out_5));
  _7_Segment_Display u_7_segment_display_2 (
    .g(n7_segment_display_1_g), .f(n7_segment_display_1_f), .a(n7_segment_display_1_a_2),
    .b(n7_segment_display_1_b_2), .e(n7_segment_display_1_e_2), .d(n7_segment_display_1_d_2),
    .c(n7_segment_display_1_c_2));  // open: dp
  xor xor_3 (xor_3_out, in_3, B[2]);
  _1_bit_adder u_1_bit_adder_3 (
    .in_1(A[2]), .in_2(xor_3_out), .in_3(n1_bit_adder_2_out_5), .out_4(out_6), .out_5(n1_bit_adder_3_out_5));
  xor xor_4 (xor_4_out, in_3, B[3]);
  _1_bit_adder u_1_bit_adder_4 (
    .in_1(A[3]), .in_2(xor_4_out), .in_3(n1_bit_adder_3_out_5), .out_4(out_5), .out_5(n1_bit_adder_4_out_5));
  _7_Segment_Display u_7_segment_display_3 (
    .g(n7_segment_display_4_g), .f(n7_segment_display_4_f), .a(n7_segment_display_4_a_2),
    .b(n7_segment_display_4_b_2), .e(n7_segment_display_4_e_2), .d(n7_segment_display_4_d_2),
    .c(n7_segment_display_4_c_2));  // open: dp
  _7_segment_display u_7_segment_display_4 (
    .A(Sum_difference), .B(out_7), .C(out_6), .D(out_5), .E(out_4), .a_2(n7_segment_display_4_a_2),
    .b_2(n7_segment_display_4_b_2), .c_2(n7_segment_display_4_c_2), .d_2(n7_segment_display_4_d_2),
    .e_2(n7_segment_display_4_e_2), .f(n7_segment_display_4_f), .g(n7_segment_display_4_g));
  buf xor_5 (out_4, n1_bit_adder_4_out_5);  // XOR_Gate

  // Notes on the sheet:
  //   Overflow / borrow
endmodule

module _7_segment_display (
  input  A,
  input  B,
  input  C,
  input  D,
  input  E,
  output a_2,
  output b_2,
  output c_2,
  output d_2,
  output e_2,
  output f,
  output g
);

  wire and_1_out, and_2_out, and_3_out, and_4_out, and_5_out, and_6_out, and_7_out, and_8_out, and_9_out,
       and_10_out, and_11_out, and_12_out, and_13_out, and_14_out, and_15_out, and_16_out, and_17_out,
       and_18_out, and_19_out, and_20_out, and_21_out, and_22_out, and_23_out, and_24_out, and_25_out,
       and_26_out, and_27_out, not_1_out, not_2_out, not_3_out, not_4_out;

  not not_1 (not_1_out, A);
  not not_2 (not_2_out, B);
  not not_3 (not_3_out, C);
  not not_4 (not_4_out, D);
  and and_1 (and_1_out, not_1_out, C);
  and and_2 (and_2_out, not_1_out, B, D);
  and and_3 (and_3_out, not_2_out, not_3_out, not_4_out);
  and and_4 (and_4_out, A, not_2_out, not_3_out);
  and and_5 (and_5_out, not_1_out, not_2_out);
  and and_6 (and_6_out, not_1_out, not_3_out, not_4_out);
  and and_7 (and_7_out, not_1_out, C, D);
  and and_8 (and_8_out, A, not_2_out, not_3_out);
  and and_9 (and_9_out, not_1_out, B);
  and and_10 (and_10_out, not_1_out, D);
  and and_11 (and_11_out, not_2_out, not_3_out, not_4_out);
  and and_12 (and_12_out, A, not_2_out, not_3_out);
  and and_13 (and_13_out, not_1_out, C, not_4_out);
  and and_14 (and_14_out, not_1_out, not_2_out, C);
  and and_15 (and_15_out, not_2_out, not_3_out, not_4_out);
  and and_16 (and_16_out, A, not_2_out, not_3_out);
  and and_17 (and_17_out, not_1_out, B, not_3_out, D);
  and and_18 (and_18_out, not_1_out, C, not_4_out);
  and and_19 (and_19_out, not_2_out, not_3_out, not_4_out);
  and and_20 (and_20_out, not_1_out, B, not_3_out);
  and and_21 (and_21_out, not_1_out, not_3_out, not_4_out);
  and and_22 (and_22_out, not_1_out, B, not_4_out);
  and and_23 (and_23_out, A, not_2_out, not_3_out);
  and and_24 (and_24_out, not_1_out, C, not_4_out);
  and and_25 (and_25_out, not_1_out, not_2_out, C);
  and and_26 (and_26_out, not_1_out, B, not_3_out);
  and and_27 (and_27_out, A, not_2_out, not_3_out);
  or or_1 (a_2, and_1_out, and_2_out, and_3_out, and_4_out);
  or or_2 (b_2, and_5_out, and_6_out, and_7_out, and_8_out);
  or or_3 (c_2, and_9_out, and_10_out, and_11_out, and_12_out);
  or or_4 (d_2, and_13_out, and_14_out, and_15_out, and_16_out, and_17_out);
  or or_5 (e_2, and_18_out, and_19_out);
  or or_6 (f, and_20_out, and_21_out, and_22_out, and_23_out);
  or or_7 (g, and_24_out, and_25_out, and_26_out, and_27_out);
endmodule

module _7_segment_test (
  input  D,
  input  C,
  input  B,
  input  A
);

  wire n7_segment_display_1_a_2, n7_segment_display_1_b_2, n7_segment_display_1_c_2,
       n7_segment_display_1_d_2, n7_segment_display_1_e_2, n7_segment_display_1_f, n7_segment_display_1_g;

  _7_segment_display u_7_segment_display_1 (
    .A(A), .B(B), .C(C), .D(D), .a_2(n7_segment_display_1_a_2), .b_2(n7_segment_display_1_b_2),
    .c_2(n7_segment_display_1_c_2), .d_2(n7_segment_display_1_d_2), .e_2(n7_segment_display_1_e_2),
    .f(n7_segment_display_1_f), .g(n7_segment_display_1_g));  // open: E
  _7_Segment_Display u_7_segment_display_2 (
    .g(n7_segment_display_1_g), .f(n7_segment_display_1_f), .a(n7_segment_display_1_a_2),
    .b(n7_segment_display_1_b_2), .e(n7_segment_display_1_e_2), .d(n7_segment_display_1_d_2),
    .c(n7_segment_display_1_c_2));  // open: dp
endmodule

module brainstorming (
  input  S,
  input  A0,
  input  B0,
  input  A1,
  input  B1,
  input  A2,
  input  B2,
  input  A3,
  input  B3,
  output S0,
  output S1,
  output S2,
  output S3,
  output C4,
  output V
);

  wire and_1_out, and_2_out, and_3_out, and_4_out, and_5_out, and_6_out, and_7_out, and_8_out, or_1_out,
       or_2_out, or_3_out, xor_1_out, xor_2_out, xor_3_out, xor_4_out, xor_5_out, xor_6_out, xor_7_out,
       xor_8_out;

  xor xor_1 (xor_1_out, S, B0);
  xor xor_2 (xor_2_out, S, B1);
  xor xor_3 (xor_3_out, S, B2);
  xor xor_4 (xor_4_out, S, B3);
  xor xor_5 (xor_5_out, A0, xor_1_out);
  and and_1 (and_1_out, A0, xor_1_out);
  xor xor_6 (xor_6_out, A1, xor_2_out);
  and and_2 (and_2_out, A1, xor_2_out);
  xor xor_7 (xor_7_out, A2, xor_3_out);
  and and_3 (and_3_out, A2, xor_3_out);
  xor xor_8 (xor_8_out, A3, xor_4_out);
  and and_4 (and_4_out, A3, xor_4_out);
  xor xor_9 (S0, S, xor_5_out);
  and and_5 (and_5_out, S, xor_5_out);
  xor xor_10 (S1, or_1_out, xor_6_out);
  and and_6 (and_6_out, or_1_out, xor_6_out);
  xor xor_11 (S2, or_2_out, xor_7_out);
  and and_7 (and_7_out, or_2_out, xor_7_out);
  xor xor_12 (S3, or_3_out, xor_8_out);
  and and_8 (and_8_out, or_3_out, xor_8_out);
  or or_1 (or_1_out, and_5_out, and_1_out);
  or or_2 (or_2_out, and_6_out, and_2_out);
  or or_3 (or_3_out, and_7_out, and_3_out);
  or or_4 (C4, and_8_out, and_4_out);
  xor xor_13 (V, or_3_out, C4);

  // Notes on the sheet:
  //   four bit full adder
  //   C0
  //   C1
  //   C2
  //   C3
endmodule

module _1_bit_adder (
  input  in_1,
  input  in_2,
  input  in_3,
  output out_4,
  output out_5
);

  wire and_1_out, and_2_out, xor_1_out;

  xor xor_1 (xor_1_out, in_2, in_3);
  and and_1 (and_1_out, in_2, in_3);
  xor xor_2 (out_4, in_1, xor_1_out);
  and and_2 (and_2_out, in_1, xor_1_out);
  or or_1 (out_5, and_2_out, and_1_out);
endmodule
