// Logisim project Assignment 13.circ as structural Verilog: 2 circuits, main circuit main
module main (
  input  in_1,
  input  _4_bit_number_1,
  input  in_3,
  input  in_4,
  input  in_5,
  input  _4_bit_number_2,
  input  in_7,
  input  in_8,
  input  in_9,
  input  in_10,
  input  in_11,
  input  in_12,
  input  in_13
);

  wire [3:0] add_sub_mul_div_1_out_11, add_sub_mul_div_1_out_12;

  Add_Sub_Mul_Div add_sub_mul_div_1 (
    .in_9({in_10, in_9}), .in_10(in_13), .in_1(in_1), .in_2(_4_bit_number_1), .in_3(in_3), .in_4(in_4),
    .in_5(in_5), .in_6(_4_bit_number_2), .in_7(in_7), .in_8(in_8), .out_11(add_sub_mul_div_1_out_11),
    .out_12(add_sub_mul_div_1_out_12));
  Hex_Digit_Display hex_digit_display_1 (.value(add_sub_mul_div_1_out_12));  // open: dp
  Hex_Digit_Display hex_digit_display_2 (.value(add_sub_mul_div_1_out_11));  // open: dp

  // Notes on the sheet:
  //   Nick Krisulevicz
  //   Assignment 13
endmodule

module Add_Sub_Mul_Div (
  input  in_1,
  input  in_2,
  input  in_3,
  input  in_4,
  input  in_5,
  input  in_6,
  input  in_7,
  input  in_8,
  input  [1:0] in_9,
  input  in_10,
  output [3:0] out_11,
  output [3:0] out_12
);

  wire adder_1_cout, subtractor_1_bout;
  wire [3:0] adder_1_out, bit_extender_1_out, bit_extender_2_out, divider_1_out, divider_1_rem,
       multiplier_1_cout, multiplier_1_out, subtractor_1_out;

  Adder #(.width(4)) adder_1 (
    .a({in_1, in_2, in_3, in_4}), .b({in_5, in_6, in_7, in_8}), .out(adder_1_out), .cout(adder_1_cout));  // open: cin
  Subtractor #(.width(4)) subtractor_1 (
    .a({in_1, in_2, in_3, in_4}), .b({in_5, in_6, in_7, in_8}), .out(subtractor_1_out),
    .bout(subtractor_1_bout));  // open: bin
  Multiplier #(.width(4)) multiplier_1 (
    .a({in_1, in_2, in_3, in_4}), .b({in_5, in_6, in_7, in_8}), .out(multiplier_1_out),
    .cout(multiplier_1_cout));  // open: cin
  Divider #(.width(4)) divider_1 (
    .a({in_1, in_2, in_3, in_4}), .b({in_5, in_6, in_7, in_8}), .out(divider_1_out), .rem(divider_1_rem));  // open: upper
  assign bit_extender_1_out = {{3{1'b0}}, adder_1_cout};  // Bit_Extender bit_extender_1
  assign bit_extender_2_out = {{3{1'b0}}, subtractor_1_bout};  // Bit_Extender bit_extender_2
  Multiplexer #(.select(2), .width(4)) multiplexer_1 (
    .in0(adder_1_out), .in1(subtractor_1_out), .in2(multiplier_1_out), .in3(divider_1_out), .out(out_11),
    .sel(in_9), .en(in_10));
  assign out_12 = bit_extender_1_out | bit_extender_2_out | multiplier_1_cout | divider_1_rem;  // OR_Gate or_1, 4 bits wide
endmodule
