// Logisim project Assignment 5.circ as structural Verilog
module main (
);


  // Notes on the sheet:
  //   Assignment 5
  //   Nick Krisulevicz
endmodule

module _1_1 (
  input  A,
  input  C_prime,
  output out_3
);

  wire not_1_out;

  not not_1 (not_1_out, C_prime);
  and and_1 (out_3, A, not_1_out);
endmodule

module _1_2 (
  input  A,
  input  B,
  input  C,
  input  D,
  output out_5
);

  wire and_1_out, and_2_out, and_3_out, and_4_out, and_5_out, not_1_out, not_2_out, not_3_out;

  not not_1 (not_1_out, A);
  not not_2 (not_2_out, A);
  not not_3 (not_3_out, A);
  and and_1 (and_1_out, not_1_out, not_2_out, D);
  and and_2 (and_2_out, not_1_out, A, D);
  and and_3 (and_3_out, not_2_out, A, D);
  and and_4 (and_4_out, A, not_3_out, D);
  and and_5 (and_5_out, A, not_2_out, D);
  or or_1 (out_5, and_1_out, and_2_out, and_3_out, and_4_out, and_5_out);

  assign B = A;
  assign C = A;
endmodule

module _1_3 (
  input  a,
  input  b,
  input  c,
  input  d,
  output out_5
);

  wire and_1_out, and_2_out, and_3_out, not_1_out;

  not not_1 (not_1_out, a);
  and and_1 (and_1_out, not_1_out, d);
  and and_2 (and_2_out, a, b, d);
  and and_3 (and_3_out, a, b, c);
  or or_1 (out_5, and_1_out, and_2_out, and_3_out);
endmodule

module _1_4 (
  input  a,
  input  b,
  input  c,
  input  d,
  output out_5
);

  wire and_1_out, and_2_out, and_3_out, and_4_out, and_5_out, not_1_out, not_2_out, not_3_out, not_4_out;

  not not_1 (not_1_out, a);
  not not_2 (not_2_out, b);
  not not_3 (not_3_out, c);
  not not_4 (not_4_out, d);
  and and_1 (and_1_out, a, b, c);
  and and_2 (and_2_out, b, not_3_out, d);
  and and_3 (and_3_out, b, c, not_4_out);
  and and_4 (and_4_out, not_1_out, not_2_out, not_3_out, not_4_out);
  and and_5 (and_5_out, not_1_out, not_2_out, c, d);
  or or_1 (out_5, and_1_out, and_2_out, and_3_out, and_4_out, and_5_out);
endmodule

module _2 (
  input  a,
  input  b,
  input  c,
  input  d,
  output out_5
);

  wire nand_1_out, nand_2_out, nand_3_out, nand_4_out, not_1_out, not_2_out, not_3_out;

  not not_1 (not_1_out, c);
  not not_2 (not_2_out, b);
  not not_3 (not_3_out, d);
  nand nand_1 (nand_1_out, b, c);
  nand nand_2 (nand_2_out, b, not_1_out, not_3_out);
  nand nand_3 (nand_3_out, not_2_out, a, d);
  nand nand_4 (nand_4_out, a, not_1_out, not_2_out);
  or or_1 (out_5, nand_1_out, nand_2_out, nand_3_out, nand_4_out);
endmodule

module _3 (
  input  a,
  input  b,
  input  c,
  output out_4
);

  wire and_1_out, and_2_out, and_3_out, not_1_out, not_2_out, not_3_out;

  not not_1 (not_1_out, b);
  not not_2 (not_2_out, a);
  not not_3 (not_3_out, c);
  and and_1 (and_1_out, not_1_out, not_3_out);
  and and_2 (and_2_out, not_2_out, c);
  and and_3 (and_3_out, not_2_out, not_3_out);
  or or_1 (out_4, and_1_out, and_2_out, and_3_out);
endmodule

module _4 (
  input  a,
  input  b,
  input  c,
  input  d,
  output out_5
);

  wire and_1_out, and_2_out, and_3_out, and_4_out, and_5_out, and_6_out, not_1_out, not_2_out, not_3_out,
       or_1_out;

  not not_1 (not_1_out, a);
  not not_2 (not_2_out, b);
  not not_3 (not_3_out, c);
  and and_1 (and_1_out, not_1_out, not_2_out, not_3_out);
  and and_2 (and_2_out, not_1_out, not_3_out, d);
  and and_3 (and_3_out, a, not_3_out, d);
  and and_4 (and_4_out, a, b, d);
  and and_5 (and_5_out, a, not_2_out, not_3_out);
  and and_6 (and_6_out, a, d, not_2_out, not_3_out);
  or or_1 (or_1_out, and_1_out, and_2_out, and_3_out, and_4_out, and_5_out);
  or or_2 (out_5, or_1_out, and_6_out);
endmodule
