// Logisim project Assignment 8.circ as structural Verilog: 7 circuits, main circuit main
module main (
);


  // Notes on the sheet:
  //   Nick Krisulevicz
  //   Assignment 8
endmodule

module _1 (
  input  A,
  input  B,
  input  C,
  input  D
);

  wire n7_segment_1_a_2, n7_segment_1_b_2, n7_segment_1_c_2, n7_segment_1_d_2, n7_segment_1_e,
       n7_segment_1_f, n7_segment_1_g;

  _7_segment u_7_segment_1 (
    .A(A), .B(B), .C(C), .D(D), .a_2(n7_segment_1_a_2), .b_2(n7_segment_1_b_2), .c_2(n7_segment_1_c_2),
    .d_2(n7_segment_1_d_2), .e(n7_segment_1_e), .f(n7_segment_1_f), .g(n7_segment_1_g));
  _7_Segment_Display u_7_segment_display_1 (
    .g(n7_segment_1_g), .f(n7_segment_1_f), .a(n7_segment_1_a_2), .b(n7_segment_1_b_2), .e(n7_segment_1_e),
    .d(n7_segment_1_d_2), .c(n7_segment_1_c_2));  // open: dp
endmodule

module _7_segment (
  input  A,
  input  B,
  input  C,
  input  D,
  output a_2,
  output b_2,
  output c_2,
  output d_2,
  output e,
  output f,
  output g
);

  wire and_1_out, and_2_out, and_3_out, and_4_out, and_5_out, and_6_out, and_7_out, and_8_out, and_9_out,
       and_10_out, and_11_out, and_12_out, and_13_out, and_14_out, and_15_out, and_16_out, and_17_out,
       and_18_out, and_19_out, and_20_out, and_21_out, and_22_out, and_23_out, and_24_out, and_25_out,
       and_26_out, and_27_out, and_28_out, and_29_out, and_30_out, and_31_out, and_32_out, not_1_out,
       not_2_out, not_3_out, not_4_out;

  not not_1 (not_1_out, A);
  not not_2 (not_2_out, B);
  not not_3 (not_3_out, C);
  not not_4 (not_4_out, D);
  and and_1 (and_1_out, not_1_out, B);
  and and_2 (and_2_out, C, not_4_out);
  and and_3 (and_3_out, not_2_out, not_3_out, not_4_out);
  and and_4 (and_4_out, not_1_out, not_2_out, C);
  and and_5 (and_5_out, A, B, C);
  and and_6 (and_6_out, not_1_out, not_2_out);
  and and_7 (and_7_out, not_1_out, C, not_4_out);
  and and_8 (and_8_out, B, not_3_out, not_4_out);
  and and_9 (and_9_out, A, B, D);
  and and_10 (and_10_out, A, not_3_out, D);
  buf and_11 (and_11_out, B);  // AND_Gate
  and and_12 (and_12_out, not_1_out, not_2_out, not_3_out);
  and and_13 (and_13_out, not_2_out, not_3_out, D);
  and and_14 (and_14_out, not_1_out, C, not_4_out);
  and and_15 (and_15_out, A, not_3_out);
  and and_16 (and_16_out, not_1_out, not_2_out, not_4_out);
  and and_17 (and_17_out, not_1_out, C, D);
  and and_18 (and_18_out, not_1_out, B, D);
  and and_19 (and_19_out, A, B, not_4_out);
  and and_20 (and_20_out, A, not_2_out);
  and and_21 (and_21_out, C, D);
  and and_22 (and_22_out, A, not_3_out);
  and and_23 (and_23_out, not_2_out, not_3_out, not_4_out);
  and and_24 (and_24_out, A, not_3_out, not_4_out);
  and and_25 (and_25_out, A, B);
  and and_26 (and_26_out, B, D);
  and and_27 (and_27_out, not_1_out, not_3_out, not_4_out);
  and and_28 (and_28_out, A, not_2_out, C);
  buf and_29 (and_29_out, A);  // AND_Gate
  and and_30 (and_30_out, B, D);
  and and_31 (and_31_out, not_1_out, not_2_out, C);
  and and_32 (and_32_out, not_1_out, B, not_3_out);
  or or_1 (a_2, and_1_out, and_2_out, and_3_out, and_4_out, and_5_out);
  or or_2 (b_2, and_6_out, and_7_out, and_8_out, and_9_out, and_10_out);
  or or_3 (c_2, and_11_out, and_12_out, and_13_out, and_14_out);
  or or_4 (d_2, and_15_out, and_16_out, and_17_out, and_18_out, and_19_out);
  or or_5 (e, and_20_out, and_21_out, and_22_out, and_23_out, and_24_out);
  or or_6 (f, and_25_out, and_26_out, and_27_out, and_28_out);
  or or_7 (g, and_29_out, and_30_out, and_31_out, and_32_out);
endmodule

module _2 (
);


  // Notes on the sheet:
  //   Got stuck on this problem
endmodule

module _3 (
  input  [1:0] XY,
  input  Z,
  input  Z_prime,
  output out_4
);

  wire and_1_out, and_2_out, and_3_out, and_4_out, decoder_1_out0, decoder_1_out1, decoder_1_out2,
       decoder_1_out3, not_1_out;

  Decoder #(.select(2)) decoder_1 (
    .out0(decoder_1_out0), .out1(decoder_1_out1), .out2(decoder_1_out2), .out3(decoder_1_out3), .sel(XY));  // open: en
  not not_1 (not_1_out, Z_prime);
  and and_1 (and_1_out, decoder_1_out0, Z);
  and and_2 (and_2_out, decoder_1_out1, not_1_out);
  and and_3 (and_3_out, decoder_1_out2, 1'b1);
  and and_4 (and_4_out, decoder_1_out3, 1'b1);
  or or_1 (out_4, and_1_out, and_2_out, and_3_out, and_4_out);
endmodule

module _4 (
  input  [1:0] AB,
  input  C,
  input  C_2,
  input  [1:0] AB_2,
  input  C_3,
  output F
);

  wire and_1_out, and_2_out, and_3_out, and_4_out, and_5_out, and_6_out, and_7_out, and_8_out,
       decoder_1_out0, decoder_1_out1, decoder_1_out2, decoder_1_out3, decoder_2_out0, decoder_2_out1,
       decoder_2_out2, decoder_2_out3, not_1_out, or_1_out, or_2_out;

  Decoder #(.select(2)) decoder_1 (
    .out0(decoder_1_out0), .out1(decoder_1_out1), .out2(decoder_1_out2), .out3(decoder_1_out3), .sel(AB));  // open: en
  not not_1 (not_1_out, C_2);
  Decoder #(.select(2)) decoder_2 (
    .out0(decoder_2_out0), .out1(decoder_2_out1), .out2(decoder_2_out2), .out3(decoder_2_out3), .sel(AB_2));  // open: en
  and and_1 (and_1_out, decoder_1_out0, C);
  and and_2 (and_2_out, decoder_1_out1, not_1_out);
  and and_3 (and_3_out, decoder_1_out2, 1'b1);
  and and_4 (and_4_out, decoder_1_out3, 1'b1);
  and and_5 (and_5_out, decoder_2_out0, C_3);
  and and_6 (and_6_out, decoder_2_out1, C_3);
  and and_7 (and_7_out, decoder_2_out2, 1'b1);
  and and_8 (and_8_out, decoder_2_out3, 1'b0);
  or or_1 (or_1_out, and_1_out, and_2_out, and_3_out, and_4_out);
  or or_2 (or_2_out, and_5_out, and_6_out, and_7_out, and_8_out);
  or or_3 (F, or_1_out, or_2_out);
endmodule

module _5 (
  input  [2:0] ABC,
  input  D,
  output F
);

  wire and_1_out, and_2_out, and_3_out, and_4_out, and_5_out, and_6_out, and_7_out, and_8_out,
       decoder_1_out0, decoder_1_out1, decoder_1_out2, decoder_1_out3, decoder_1_out4, decoder_1_out5,
       decoder_1_out6, decoder_1_out7, not_1_out;

  not not_1 (not_1_out, D);
  Decoder #(.select(3)) decoder_1 (
    .out0(decoder_1_out0), .out1(decoder_1_out1), .out2(decoder_1_out2), .out3(decoder_1_out3),
    .out4(decoder_1_out4), .out5(decoder_1_out5), .out6(decoder_1_out6), .out7(decoder_1_out7), .sel(ABC));  // open: en
  and and_1 (and_1_out, D, decoder_1_out0);
  and and_2 (and_2_out, D, decoder_1_out1);
  and and_3 (and_3_out, D, decoder_1_out2);
  and and_4 (and_4_out, D, decoder_1_out3);
  and and_5 (and_5_out, not_1_out, decoder_1_out4);
  and and_6 (and_6_out, 1'b1, decoder_1_out5);
  and and_7 (and_7_out, 1'b1, decoder_1_out6);
  and and_8 (and_8_out, 1'b0, decoder_1_out7);
  or or_1 (F, and_1_out, and_2_out, and_3_out, and_4_out, and_5_out, and_6_out, and_7_out, and_8_out);
endmodule
