// Logisim project Assignment 9.circ as structural Verilog: 4 circuits, main circuit main
module main (
);


  // Notes on the sheet:
  //   Nick Krisulevicz
  //   Assignment 9
  //   11/04/2020
endmodule

module _1 (
  input  D,
  input  [2:0] ABC,
  output F
);

  wire not_1_out;

  not not_1 (not_1_out, D);
  Multiplexer #(.select(3)) multiplexer_1 (
    .in0(D), .in1(1'b1), .in2(D), .in3(D), .in4(1'b0), .in5(not_1_out), .in6(D), .in7(D), .out(F), .sel(ABC));  // open: en

  // Notes on the sheet:
  //   8-1 MUX
endmodule

module _2 (
  input  D,
  input  [2:0] ABC,
  output F
);

  wire not_1_out;

  not not_1 (not_1_out, D);
  Multiplexer #(.select(3)) multiplexer_1 (
    .in0(1'b0), .in1(not_1_out), .in2(D), .in3(not_1_out), .in4(1'b0), .in5(D), .in6(not_1_out), .in7(1'b1),
    .out(F), .sel(ABC));  // open: en

  // Notes on the sheet:
  //   8-1 MUX
endmodule

module _3 (
  input  [2:0] in_1,
  output out_2
);

  wire decoder_1_out0, decoder_1_out1, decoder_1_out2, decoder_1_out3, decoder_1_out4, decoder_1_out5,
       decoder_1_out6, decoder_1_out7;

  Decoder #(.select(3)) decoder_1 (
    .out0(decoder_1_out0), .out1(decoder_1_out1), .out2(decoder_1_out2), .out3(decoder_1_out3),
    .out4(decoder_1_out4), .out5(decoder_1_out5), .out6(decoder_1_out6), .out7(decoder_1_out7));  // open: sel, en
  // AND_Gate and_1 has open pins: in0=decoder_1_out7, in1=decoder_1_out6, out=open
  // AND_Gate and_2 has open pins: in0=decoder_1_out7, in1=decoder_1_out5, out=open
  // AND_Gate and_3 has open pins: in0=decoder_1_out7, in1=decoder_1_out4, out=open
  // AND_Gate and_4 has open pins: in0=decoder_1_out7, in1=decoder_1_out3, out=open
  // AND_Gate and_5 is placed but not wired
  // AND_Gate and_6 is placed but not wired
  // AND_Gate and_7 is placed but not wired
  // AND_Gate and_8 is placed but not wired
  // OR_Gate or_1 has open pins: out=out_2
endmodule
