// Logisim project Classwork 10-29 - DEMUX.circ as structural Verilog
module classwork (
  input  in_1,
  input  in_2,
  input  E,
  input  E_2,
  input  B,
  input  A,
  input  C,
  input  B_2,
  input  A_2,
  output _1_4_DMX,
  output out_11,
  output out_12,
  output out_13,
  output D0,
  output D0_2,
  output D1,
  output D1_2,
  output D2,
  output D2_2,
  output D3,
  output D3_2,
  output D4,
  output D5,
  output D6,
  output D7
);

  wire not_1_out, not_2_out, not_3_out, not_4_out, not_5_out;

  not not_1 (not_1_out, B);
  Demultiplexer demultiplexer_1 (.out0(out_11), .out1(out_13), .in(in_1), .en(in_2));  // open: sel
  not not_2 (not_2_out, A);
  and and_1 (D0, E, not_1_out, not_2_out);
  and and_2 (D1, E, not_2_out, B);
  and and_3 (D2, E, A, not_1_out);
  and and_4 (D3, E, A, B);
  not not_3 (not_3_out, C);
  not not_4 (not_4_out, B_2);
  not not_5 (not_5_out, A_2);
  and and_5 (D0_2, E_2, not_5_out, not_4_out, not_3_out);
  and and_6 (D1_2, E_2, not_5_out, not_4_out, C);
  and and_7 (D2_2, E_2, not_5_out, B_2, not_3_out);
  and and_8 (D3_2, E_2, not_5_out, B_2, C);
  and and_9 (D4, E_2, A_2, not_4_out, not_3_out);
  and and_10 (D5, E_2, A_2, not_4_out, C);
  and and_11 (D6, E_2, A_2, B_2, not_3_out);
  and and_12 (D7, E_2, A_2, B_2, C);

  // Notes on the sheet:
  //   1-4 DMX
  //   A=0 B=0
  //   A=0 B=1
  //   A=1 B=0
  //   A=1 B=1
  //   1-8 DMX
  //   A=0 B=0 C=0
  //   A=0 B=0 C=1
  //   A=0 B=1 C=0
  //   A=0 B=1 C=1
  //   A=1 B=0 C=0
  //   A=1 B=0 C=1
  //   A=1 B=1 C=0
  //   A=1 B=1 C=1
endmodule
