// Logisim project Classwork 11-03 - ADDERS.circ as structural Verilog: 5 circuits, main circuit main
module main (
);


  // Notes on the sheet:
  //   11/03/2020
  //   Nick Krisulevicz
  //   Half adder and full adder file
endmodule

module half_adder (
  input  C,
  input  A,
  input  B,
  output S,
  output C_1
);

  Adder #(.width(1)) adder_1 (.a(A), .b(B), .out(S), .cin(C), .cout(C_1));
endmodule

module half_adder_only_gates (
  input  A,
  input  B,
  output S,
  output C_1
);

  xor xor_1 (S, A, B);
  and and_1 (C_1, A, B);
endmodule

module full_adder_only_gates (
  input  C,
  input  A,
  input  B,
  output S,
  output C_1
);

  wire and_1_out, and_2_out, xor_1_out;

  xor xor_1 (xor_1_out, A, B);
  and and_1 (and_1_out, A, B);
  xor xor_2 (S, C, xor_1_out);
  and and_2 (and_2_out, C, xor_1_out);
  or or_1 (C_1, and_2_out, and_1_out);
endmodule

module full_adder_with_blocks (
  input  A,
  input  B,
  input  C,
  output S,
  output C_1
);

  wire half_adder_only_gates_1_c_1, half_adder_only_gates_1_s, half_adder_only_gates_2_s;

  half_adder_only_gates half_adder_only_gates_1 (
    .A(A), .B(B), .S(half_adder_only_gates_1_s), .C_1(half_adder_only_gates_1_c_1));
  half_adder_only_gates half_adder_only_gates_2 (
    .A(half_adder_only_gates_1_c_1), .B(C), .S(half_adder_only_gates_2_s), .C_1(C_1));
  or or_1 (S, half_adder_only_gates_1_s, half_adder_only_gates_2_s);

  // Notes on the sheet:
  //   HA
  //   HA
endmodule
