// Logisim project Classwork 11-19 - SYNCHRONOUS COUNTERS.circ as structural Verilog
module main (
  input  INPUT,
  output Q2,
  output Q1,
  output Q0
);

  wire and_1_out, and_2_out, clock_1_out, not_1_out;

  Clock clock_1 (.out(clock_1_out));
  not not_1 (not_1_out, and_1_out);
  and and_1 (and_1_out, Q0, Q2);
  J_K_Flip_Flop j_k_ff_1 (.J(INPUT), .clk(clock_1_out), .K(INPUT), .Q(Q0), .reset(not_1_out));  // open: Qn, preset, en
  and and_2 (and_2_out, Q0, Q1);
  J_K_Flip_Flop j_k_ff_2 (.J(Q0), .clk(clock_1_out), .K(Q0), .Q(Q1), .reset(not_1_out));  // open: Qn, preset, en
  J_K_Flip_Flop j_k_ff_3 (
    .J(and_2_out), .clk(clock_1_out), .K(and_2_out), .Q(Q2), .reset(not_1_out));  // open: Qn, preset, en

  // Notes on the sheet:
  //   CLOCK
endmodule

module base_3_counter (
  input  INPUT,
  input  RESET,
  output Q0,
  output Q1,
  output Q2
);

  wire and_1_out, clock_1_out;

  Clock clock_1 (.out(clock_1_out));
  J_K_Flip_Flop j_k_ff_1 (.J(INPUT), .clk(clock_1_out), .K(INPUT), .Q(Q0), .reset(RESET));  // open: Qn, preset, en
  and and_1 (and_1_out, Q0, Q1);
  J_K_Flip_Flop j_k_ff_2 (.J(Q0), .clk(clock_1_out), .K(Q0), .Q(Q1), .reset(RESET));  // open: Qn, preset, en
  J_K_Flip_Flop j_k_ff_3 (
    .J(and_1_out), .clk(clock_1_out), .K(and_1_out), .Q(Q2), .reset(RESET));  // open: Qn, preset, en

  // Notes on the sheet:
  //   CLOCK
endmodule

module BCD_4_bit_synchronous_counter (
  input  in_1,
  input  in_2,
  output out_3,
  output out_4,
  output out_5,
  output out_6
);

  wire and_1_out, and_2_out, and_3_out, and_4_out, clock_1_out, not_1_out, or_1_out;

  Clock clock_1 (.out(clock_1_out));
  J_K_Flip_Flop j_k_ff_1 (.J(in_1), .clk(clock_1_out), .K(in_1), .Q(out_6), .reset(in_2));  // open: Qn, preset, en
  not not_1 (not_1_out, out_3);
  and and_1 (and_1_out, not_1_out, out_6);
  J_K_Flip_Flop j_k_ff_2 (
    .J(and_1_out), .clk(clock_1_out), .K(and_1_out), .Q(out_5), .reset(in_2));  // open: Qn, preset, en
  and and_2 (and_2_out, out_6, out_5);
  J_K_Flip_Flop j_k_ff_3 (
    .J(and_2_out), .clk(clock_1_out), .K(and_2_out), .Q(out_4), .reset(in_2));  // open: Qn, preset, en
  and and_3 (and_3_out, out_6, and_1_out, out_4);
  and and_4 (and_4_out, out_6, out_3);
  J_K_Flip_Flop j_k_ff_4 (
    .J(or_1_out), .clk(clock_1_out), .K(or_1_out), .Q(out_3), .reset(in_2));  // open: Qn, preset, en
  or or_1 (or_1_out, and_3_out, and_4_out);
endmodule
