// Logisim project LAB 10.circ as structural Verilog: 5 circuits, main circuit main
module main (
);


  // Notes on the sheet:
  //   Lab 10
  //   11/04/2020
  //   Nick Krisulevicz
endmodule

module full_adder (
  input  A,
  input  B,
  input  C,
  output S,
  output C_1
);

  wire half_adder_1_c_1, half_adder_1_s, half_adder_2_s;

  half_adder half_adder_1 (.A(A), .B(B), .S(half_adder_1_s), .C_1(half_adder_1_c_1));  // open: C
  half_adder half_adder_2 (.A(half_adder_1_c_1), .B(C), .S(half_adder_2_s), .C_1(C_1));  // open: C
  or or_1 (S, half_adder_1_s, half_adder_2_s);

  // Notes on the sheet:
  //   HA
  //   HA
endmodule

module half_adder (
  input  C,
  input  A,
  input  B,
  output S,
  output C_1
);

  Adder #(.width(1)) adder_1 (.a(A), .b(B), .out(S), .cin(C), .cout(C_1));
endmodule

module _4_bit_full_adder (
  input  C,
  input  A,
  input  B,
  input  A_2,
  input  B_2,
  input  A_3,
  input  B_3,
  input  A_4,
  input  B_4,
  output S,
  output S_2,
  output S_3,
  output S_4,
  output S_5
);

  wire adder_1_cout, adder_2_cout, adder_3_cout;

  Adder #(.width(1)) adder_1 (.a(A), .b(B), .out(S), .cin(C), .cout(adder_1_cout));
  Adder #(.width(1)) adder_2 (.a(A_2), .b(B_2), .out(S_2), .cin(adder_1_cout), .cout(adder_2_cout));
  Adder #(.width(1)) adder_3 (.a(A_3), .b(B_3), .out(S_3), .cin(adder_2_cout), .cout(adder_3_cout));
  Adder #(.width(1)) adder_4 (.a(A_4), .b(B_4), .out(S_4), .cin(adder_3_cout), .cout(S_5));

  // Notes on the sheet:
  //   4 BIT FULL ADDER
endmodule

module subtractor (
  input  A,
  input  B,
  input  A_2,
  input  B_2,
  input  A_3,
  input  B_3,
  input  A_4,
  input  B_4,
  output S,
  output S_2,
  output S_3,
  output S_4,
  output S_5
);

  wire adder_1_cout, adder_2_cout, adder_3_cout, not_1_out, not_2_out, not_3_out, not_4_out;

  not not_1 (not_1_out, B);
  not not_2 (not_2_out, B_2);
  not not_3 (not_3_out, B_3);
  not not_4 (not_4_out, B_4);
  Adder #(.width(1)) adder_1 (.a(A), .b(not_1_out), .out(S), .cin(1'b1), .cout(adder_1_cout));
  Adder #(.width(1)) adder_2 (.a(A_2), .b(not_2_out), .out(S_2), .cin(adder_1_cout), .cout(adder_2_cout));
  Adder #(.width(1)) adder_3 (.a(A_3), .b(not_3_out), .out(S_3), .cin(adder_2_cout), .cout(adder_3_cout));
  Adder #(.width(1)) adder_4 (.a(A_4), .b(not_4_out), .out(S_4), .cin(adder_3_cout), .cout(S_5));

  // Notes on the sheet:
  //   4 BIT SUBTRACTOR
  //   C
endmodule
