// Logisim project LAB 12.circ as structural Verilog: 10 circuits, main circuit main
module main (
);


  // Notes on the sheet:
  //   Nick Krisulevicz
  //   Lab 12
  //   11/18/2020
endmodule

module _4_D_flip_flop_register (
  input  RESET,
  input  CLOCK,
  input  in_3,
  input  in_4,
  input  in_5,
  output Q0,
  output out_7,
  output Q1,
  output out_9,
  output Q2,
  output out_11,
  output Q3,
  output out_13
);

  wire clock_1_out;

  Clock clock_1 (.out(clock_1_out));
  D_Flip_Flop d_ff_1 (.clk(clock_1_out), .D(CLOCK), .Q(Q0), .Qn(out_7), .reset(RESET));  // open: preset, en
  D_Flip_Flop d_ff_2 (.clk(clock_1_out), .D(in_3), .Q(Q1), .Qn(out_9), .reset(RESET));  // open: preset, en
  D_Flip_Flop d_ff_3 (.clk(clock_1_out), .D(in_4), .Q(Q2), .Qn(out_11), .reset(RESET));  // open: preset, en
  D_Flip_Flop d_ff_4 (.clk(clock_1_out), .D(in_5), .Q(Q3), .Qn(out_13), .reset(RESET));  // open: preset, en
endmodule

module _4_D_flip_flop_register_with_parallel_load (
  input  RESET,
  input  LOAD,
  input  in_3,
  input  in_4,
  input  in_5,
  input  in_6,
  output Q0,
  output out_8,
  output Q1,
  output out_10,
  output Q2,
  output out_12,
  output Q3,
  output out_14
);

  wire clock_1_out, not_1_out, or_1_out;

  Clock clock_1 (.out(clock_1_out));
  not not_1 (not_1_out, LOAD);
  or or_1 (or_1_out, not_1_out, clock_1_out);
  D_Flip_Flop d_ff_1 (.clk(or_1_out), .D(in_3), .Q(Q0), .Qn(out_8), .reset(RESET));  // open: preset, en
  D_Flip_Flop d_ff_2 (.clk(or_1_out), .D(in_4), .Q(Q1), .Qn(out_10), .reset(RESET));  // open: preset, en
  D_Flip_Flop d_ff_3 (.clk(or_1_out), .D(in_5), .Q(Q2), .Qn(out_12), .reset(RESET));  // open: preset, en
  D_Flip_Flop d_ff_4 (.clk(or_1_out), .D(in_6), .Q(Q3), .Qn(out_14), .reset(RESET));  // open: preset, en

  // Notes on the sheet:
  //   CLOCK
endmodule

module _4_D_flip_flop_register_with_load_in_inputs (
  input  LOAD,
  input  in_2,
  input  in_3,
  input  in_4,
  input  in_5,
  output Q0,
  output out_7,
  output Q1,
  output out_9,
  output Q2,
  output out_11,
  output Q3,
  output out_13
);

  wire and_1_out, and_2_out, and_3_out, and_4_out, and_5_out, and_6_out, and_7_out, and_8_out, clock_1_out,
       not_1_out, or_1_out, or_2_out, or_3_out, or_4_out;

  not not_1 (not_1_out, LOAD);
  Clock clock_1 (.out(clock_1_out));
  and and_1 (and_1_out, Q0, not_1_out);
  and and_2 (and_2_out, in_2, LOAD);
  and and_3 (and_3_out, Q1, not_1_out);
  and and_4 (and_4_out, in_3, LOAD);
  and and_5 (and_5_out, Q2, not_1_out);
  and and_6 (and_6_out, in_4, LOAD);
  and and_7 (and_7_out, Q3, not_1_out);
  and and_8 (and_8_out, in_5, LOAD);
  or or_1 (or_1_out, and_1_out, and_2_out);
  or or_2 (or_2_out, and_3_out, and_4_out);
  or or_3 (or_3_out, and_5_out, and_6_out);
  or or_4 (or_4_out, and_7_out, and_8_out);
  D_Flip_Flop d_ff_1 (.clk(clock_1_out), .D(or_1_out), .Q(Q0), .Qn(out_7));  // open: preset, en, reset
  D_Flip_Flop d_ff_2 (.clk(clock_1_out), .D(or_2_out), .Q(Q1), .Qn(out_9));  // open: preset, en, reset
  D_Flip_Flop d_ff_3 (.clk(clock_1_out), .D(or_3_out), .Q(Q2), .Qn(out_11));  // open: preset, en, reset
  D_Flip_Flop d_ff_4 (.clk(clock_1_out), .D(or_4_out), .Q(Q3), .Qn(out_13));  // open: preset, en, reset

  // Notes on the sheet:
  //   CLOCK
endmodule

module _4_JK_flip_flop_register (
  input  in_1,
  input  in_2,
  input  in_3,
  input  in_4,
  input  in_5,
  input  in_6,
  input  in_7,
  input  LOAD,
  input  in_9,
  input  RESET,
  output Q0,
  output out_12,
  output Q1,
  output out_14,
  output Q2,
  output out_16,
  output Q3,
  output out_18
);

  wire clock_1_out, not_1_out, or_1_out;

  Clock clock_1 (.out(clock_1_out));
  not not_1 (not_1_out, LOAD);
  or or_1 (or_1_out, not_1_out, clock_1_out);
  J_K_Flip_Flop j_k_ff_1 (.J(in_1), .clk(or_1_out), .K(in_2), .Q(Q0), .Qn(out_12), .reset(RESET));  // open: preset, en
  J_K_Flip_Flop j_k_ff_2 (.J(in_3), .clk(or_1_out), .K(in_4), .Q(Q1), .Qn(out_14), .reset(RESET));  // open: preset, en
  J_K_Flip_Flop j_k_ff_3 (.J(in_5), .clk(or_1_out), .K(in_6), .Q(Q2), .Qn(out_16), .reset(RESET));  // open: preset, en
  J_K_Flip_Flop j_k_ff_4 (.J(in_7), .clk(or_1_out), .K(in_9), .Q(Q3), .Qn(out_18), .reset(RESET));  // open: preset, en

  // Notes on the sheet:
  //   CLOCK
endmodule

module _4_JK_flip_flop_register_behaves_like_D (
  input  in_1,
  input  in_2,
  input  in_3,
  input  in_4,
  input  LOAD,
  input  RESET,
  output Q0,
  output out_8,
  output Q1,
  output out_10,
  output Q2,
  output out_12,
  output Q3,
  output out_14
);

  wire clock_1_out, not_1_out, not_2_out, not_3_out, not_4_out, not_5_out, or_1_out;

  Clock clock_1 (.out(clock_1_out));
  not not_1 (not_1_out, LOAD);
  or or_1 (or_1_out, not_1_out, clock_1_out);
  not not_2 (not_2_out, in_1);
  not not_3 (not_3_out, in_2);
  not not_4 (not_4_out, in_3);
  not not_5 (not_5_out, in_4);
  J_K_Flip_Flop j_k_ff_1 (
    .J(in_1), .clk(or_1_out), .K(not_2_out), .Q(Q0), .Qn(out_8), .reset(RESET));  // open: preset, en
  J_K_Flip_Flop j_k_ff_2 (
    .J(in_2), .clk(or_1_out), .K(not_3_out), .Q(Q1), .Qn(out_10), .reset(RESET));  // open: preset, en
  J_K_Flip_Flop j_k_ff_3 (
    .J(in_3), .clk(or_1_out), .K(not_4_out), .Q(Q2), .Qn(out_12), .reset(RESET));  // open: preset, en
  J_K_Flip_Flop j_k_ff_4 (
    .J(in_4), .clk(or_1_out), .K(not_5_out), .Q(Q3), .Qn(out_14), .reset(RESET));  // open: preset, en

  // Notes on the sheet:
  //   CLOCK
endmodule

module Shift_register (
  input  SERIAL_INPUT,
  input  RESET,
  output SERIAL_OUTPUT
);

  wire clock_1_out, d_ff_1_q, d_ff_2_q, d_ff_3_q;

  Clock clock_1 (.out(clock_1_out));
  D_Flip_Flop d_ff_1 (.clk(clock_1_out), .D(SERIAL_INPUT), .Q(d_ff_1_q), .reset(RESET));  // open: Qn, preset, en
  D_Flip_Flop d_ff_2 (.clk(clock_1_out), .D(d_ff_1_q), .Q(d_ff_2_q), .reset(RESET));  // open: Qn, preset, en
  D_Flip_Flop d_ff_3 (.clk(clock_1_out), .D(d_ff_2_q), .Q(d_ff_3_q), .reset(RESET));  // open: Qn, preset, en
  D_Flip_Flop d_ff_4 (.clk(clock_1_out), .D(d_ff_3_q), .Q(SERIAL_OUTPUT), .reset(RESET));  // open: Qn, preset, en

  // Notes on the sheet:
  //   CLOCK
endmodule

module Shift_register_with_parallel_load (
  input  LOAD,
  input  SHIFT,
  input  SERIAL_INPUT,
  input  in_4,
  input  in_5,
  input  in_6,
  input  in_7,
  input  RESET,
  output Q0,
  output Q1,
  output Q2,
  output Q3
);

  wire and_1_out, and_2_out, and_3_out, and_4_out, and_5_out, and_6_out, and_7_out, and_8_out, and_9_out,
       and_10_out, and_11_out, and_12_out, clock_1_out, not_1_out, not_2_out, or_1_out, or_2_out, or_3_out,
       or_4_out;

  Clock clock_1 (.out(clock_1_out));
  not not_1 (not_1_out, LOAD);
  not not_2 (not_2_out, SHIFT);
  and and_1 (and_1_out, SERIAL_INPUT, SHIFT);
  and and_2 (and_2_out, not_2_out, in_4, LOAD);
  and and_3 (and_3_out, not_2_out, not_1_out, Q0);
  and and_4 (and_4_out, Q0, SHIFT);
  and and_5 (and_5_out, not_2_out, in_5, LOAD);
  and and_6 (and_6_out, not_2_out, not_1_out, Q1);
  and and_7 (and_7_out, Q1, SHIFT);
  and and_8 (and_8_out, not_2_out, in_6, LOAD);
  and and_9 (and_9_out, not_2_out, not_1_out, Q2);
  and and_10 (and_10_out, Q2, SHIFT);
  and and_11 (and_11_out, not_2_out, in_7, LOAD);
  and and_12 (and_12_out, not_2_out, not_1_out, Q3);
  or or_1 (or_1_out, and_1_out, and_2_out, and_3_out);
  or or_2 (or_2_out, and_4_out, and_5_out, and_6_out);
  or or_3 (or_3_out, and_7_out, and_8_out, and_9_out);
  or or_4 (or_4_out, and_10_out, and_11_out, and_12_out);
  D_Flip_Flop d_ff_1 (.clk(clock_1_out), .D(or_1_out), .Q(Q0), .reset(RESET));  // open: Qn, preset, en
  D_Flip_Flop d_ff_2 (.clk(clock_1_out), .D(or_2_out), .Q(Q1), .reset(RESET));  // open: Qn, preset, en
  D_Flip_Flop d_ff_3 (.clk(clock_1_out), .D(or_3_out), .Q(Q2), .reset(RESET));  // open: Qn, preset, en
  D_Flip_Flop d_ff_4 (.clk(clock_1_out), .D(or_4_out), .Q(Q3), .reset(RESET));  // open: Qn, preset, en

  // Notes on the sheet:
  //   CLOCK
endmodule

module Serial_adder_with_shift_register (
  input  in_1
);

  wire clock_1_out, not_1_out, or_1_out;

  Clock clock_1 (.out(clock_1_out));
  not not_1 (not_1_out, in_1);
  or or_1 (or_1_out, not_1_out, clock_1_out);
  Shift_Register #(.length(4)) shift_register_1 (.clk(or_1_out));  // open: shift, in, out, load, clr, d0, q0, d1, q1, d2, q2, d3, q3
endmodule

module Ripple_counter (
  input  SERIAL_INPUT,
  output out_2,
  output out_3,
  output out_4,
  output out_5
);

  wire clock_1_out;

  Clock clock_1 (.out(clock_1_out));
  J_K_Flip_Flop j_k_ff_1 (
    .J(SERIAL_INPUT), .clk(clock_1_out), .K(SERIAL_INPUT), .Q(out_2));  // open: Qn, preset, en, reset
  J_K_Flip_Flop j_k_ff_2 (.J(SERIAL_INPUT), .clk(out_2), .K(SERIAL_INPUT), .Q(out_3));  // open: Qn, preset, en, reset
  J_K_Flip_Flop j_k_ff_3 (.J(SERIAL_INPUT), .clk(out_3), .K(SERIAL_INPUT), .Q(out_4));  // open: Qn, preset, en, reset
  J_K_Flip_Flop j_k_ff_4 (.J(SERIAL_INPUT), .clk(out_4), .K(SERIAL_INPUT), .Q(out_5));  // open: Qn, preset, en, reset

  // Notes on the sheet:
  //   CLOCK
endmodule
