// Logisim project LAB 2.circ as structural Verilog: 1 circuit, main circuit main
module main (
  input  in_1,
  input  in_2,
  input  in_3,
  input  in_4,
  input  in_5,
  input  in_6,
  input  in_7,
  input  in_8,
  input  in_9,
  input  in_10,
  input  in_11,
  input  in_12,
  input  in_13,
  input  in_14,
  input  in_15,
  input  in_16,
  input  in_17,
  input  in_18,
  input  in_19,
  input  in_20,
  input  in_21,
  input  in_22,
  output out_23,
  output out_24,
  output out_25,
  output out_26,
  output out_27,
  output out_28,
  output NOT_gate,
  output out_30,
  output out_31,
  output out_32,
  output out_33,
  output out_34
);

  wire and_1_out, and_2_out, and_3_out, nand_2_out, nand_3_out, nand_4_out, nand_5_out, nand_7_out,
       nand_8_out, nand_9_out, nand_10_out, nand_13_out, nand_14_out, nor_1_out, nor_2_out, nor_3_out,
       nor_5_out, nor_6_out, nor_8_out, nor_9_out, not_1_out, not_2_out;

  not not_1 (not_1_out, in_1);
  not not_2 (not_2_out, in_3);
  and and_1 (and_1_out, not_1_out, in_3);
  and and_2 (and_2_out, in_1, not_2_out);
  nand nand_1 (out_25, in_5, in_5, in_7);
  and and_3 (and_3_out, in_8, in_10);
  not not_3 (NOT_gate, in_12);
  not nand_2 (nand_2_out, in_13);  // NAND_Gate
  not nand_3 (nand_3_out, in_15);  // NAND_Gate
  nor nor_1 (nor_1_out, in_17, in_17);
  nor nor_2 (nor_2_out, in_21, in_21);
  or or_1 (out_23, and_1_out, and_2_out);
  not not_4 (out_27, and_3_out);
  nand nand_4 (nand_4_out, nand_2_out, nand_2_out);
  not nand_5 (nand_5_out, nand_3_out);  // NAND_Gate
  nor nor_3 (nor_3_out, nor_1_out, nor_2_out);
  nand nand_6 (out_30, nand_4_out, nand_5_out);
  not nor_4 (out_32, nor_3_out);  // NOR_Gate
  nand nand_7 (nand_7_out, in_2, in_4);
  nand nand_8 (nand_8_out, in_2, in_4, in_4);
  nand nand_9 (nand_9_out, in_9, in_11);
  nand nand_10 (nand_10_out, nand_7_out, nand_8_out);
  nand nand_11 (out_26, in_6, in_6);
  nand nand_12 (out_28, nand_9_out, nand_9_out);
  nand nand_13 (nand_13_out, in_14, in_14);
  nand nand_14 (nand_14_out, in_16, in_16);
  nor nor_5 (nor_5_out, in_18, in_18);
  nor nor_6 (nor_6_out, in_20, in_20);
  not nand_15 (out_24, nand_10_out);  // NAND_Gate
  nand nand_16 (out_31, nand_13_out, nand_14_out);
  nor nor_7 (out_33, nor_5_out, nor_6_out);
  nor nor_8 (nor_8_out, in_19, in_19, in_22);
  nor nor_9 (nor_9_out, in_19, in_22, in_22);
  nor nor_10 (out_34, nor_8_out, nor_9_out);

  // Notes on the sheet:
  //   Nick Krisulevicz
  //   Lab 2
  //   NOT gate using NOR gates
  //   AND gate circuit
  //   Attempt at inverter with NAND gate
  //   XOR circuit built using Logisim
  //   NAND gate circuit
  //   AND gate using NOR gates
  //   Attempt at inverter with NAND gate
  //   Inverter with NAND gate
  //   AND gate made with NAND gates
  //   OR gate using NAND
  //   OR gate using NOR gates
endmodule
