// Logisim project LAB 3.circ as structural Verilog: 3 circuits, main circuit main
module main (
  input  in_1,
  input  in_2,
  input  in_3,
  input  in_4,
  input  in_5,
  input  in_6,
  input  in_7,
  input  in_8,
  input  in_9,
  input  in_10,
  output out_11,
  output out_12
);

  wire and_1_out, and_2_out, and_3_out, and_4_out, and_5_out, or_1_out;

  and and_1 (and_1_out, in_6, in_7);
  and and_2 (and_2_out, in_8, in_9);
  and and_3 (and_3_out, in_2, in_3);
  buf or_1 (or_1_out, and_1_out);  // OR_Gate
  and and_4 (and_4_out, and_2_out, in_10);
  and and_5 (and_5_out, and_3_out, in_4);
  or or_2 (out_12, or_1_out, and_4_out);
  or or_3 (out_11, in_1, and_5_out, in_5);
endmodule

module _2_4a (
  input  A,
  input  _1,
  input  E,
  input  B,
  input  C,
  input  D,
  input  A_2,
  input  B_2,
  input  C_2,
  input  D_2,
  input  E_2,
  output F,
  output F_2
);

  wire and_1_out, and_2_out, and_3_out, and_4_out, and_5_out, or_1_out, or_2_out;

  and and_1 (and_1_out, A, _1);
  and and_2 (and_2_out, B_2, C_2);
  or or_1 (or_1_out, and_1_out, and_1_out);
  and and_3 (and_3_out, B, C);
  and and_4 (and_4_out, and_3_out, D);
  and and_5 (and_5_out, and_2_out, D_2);
  or or_2 (or_2_out, or_1_out, E);
  or or_3 (F_2, A_2, and_5_out, E_2);
  or or_4 (F, or_2_out, and_4_out);

  // Notes on the sheet:
  //   Problem 2.4 a
  //   Simplified circuit
endmodule

module _2_4_b (
  input  A,
  input  B,
  input  B_2,
  input  A_2,
  input  B_3,
  input  A_3,
  input  B_4,
  output out_8
);

  wire and_1_out, and_2_out, and_3_out, not_1_out, or_1_out, or_2_out;

  not not_1 (not_1_out, B);
  and and_1 (and_1_out, A, not_1_out);
  and and_2 (and_2_out, A_2, B_4);
  or or_1 (or_1_out, B_2, and_2_out);
  or or_2 (or_2_out, and_1_out, or_1_out);
  and and_3 (and_3_out, or_2_out, B_3);
  or or_3 (out_8, and_3_out, A_3);

  // Notes on the sheet:
  //   Problem 2.4b
endmodule
