// Logisim project LAB 4.circ as structural Verilog: 4 circuits, main circuit main
module main (
  input  A,
  input  B,
  input  C,
  input  D,
  output out_5
);

  wire and_1_out, not_1_out, not_2_out, or_1_out, or_2_out;

  or or_1 (or_1_out, A, B);
  not not_1 (not_1_out, C);
  not not_2 (not_2_out, or_1_out);
  or or_2 (or_2_out, C, D);
  and and_1 (and_1_out, not_2_out, or_2_out);
  or or_3 (out_5, and_1_out, not_1_out);

  // Notes on the sheet:
  //   Nick Krisulevicz
  //   Lab 4
  //   09/23/2020
  //   Exercise 2.b
endmodule

module example_2 (
  input  in_1,
  input  in_2,
  input  in_3,
  input  in_4,
  output out_5
);

  wire and_1_out, and_2_out, and_3_out, and_4_out, or_1_out, or_2_out;

  and and_1 (and_1_out, in_1, in_2);
  and and_2 (and_2_out, in_1, in_3, in_4);
  and and_3 (and_3_out, in_2, in_3, in_4);
  and and_4 (and_4_out, in_2, in_4);
  or or_1 (or_1_out, and_1_out, and_2_out);
  or or_2 (or_2_out, and_3_out, and_4_out);
  or or_3 (out_5, or_1_out, or_2_out);

  // Notes on the sheet:
  //   Example 2
endmodule

module Exercise_7 (
  input  B,
  input  A,
  input  C,
  output F
);

  wire and_1_out, not_1_out, not_2_out, not_3_out;

  not not_1 (not_1_out, A);
  not not_2 (not_2_out, C);
  not not_3 (not_3_out, B);
  and and_1 (and_1_out, not_1_out, not_2_out);
  or or_1 (F, not_3_out, and_1_out);

  // Notes on the sheet:
  //   Exercise 7
endmodule

module Example_4 (
  input  in_1,
  input  in_2,
  input  in_3,
  output out_4
);

  wire and_1_out, and_2_out, and_3_out, not_1_out, not_2_out, or_1_out;

  not not_1 (not_1_out, in_1);
  and and_1 (and_1_out, not_1_out, in_2, in_3);
  and and_2 (and_2_out, in_1, in_3);
  and and_3 (and_3_out, in_2, in_3);
  not not_2 (not_2_out, and_1_out);
  or or_1 (or_1_out, not_2_out, and_2_out);
  or or_2 (out_4, or_1_out, and_3_out);

  // Notes on the sheet:
  //   Example 4
endmodule
