// Logisim project LAB 7.circ as structural Verilog: 3 circuits, main circuit main
module main (
  input  A,
  input  B,
  input  C,
  input  D,
  input  A_2,
  input  B_2,
  input  C_2,
  input  D_2,
  input  in_9,
  input  in_10,
  output out_11,
  output out_12,
  output out_13,
  output out_14
);

  wire nor_2_out, nor_3_out, nor_4_out, not_1_out, not_3_out, not_4_out, not_5_out, not_6_out, not_7_out,
       not_8_out, not_9_out, or_1_out, or_2_out, or_3_out;

  not not_1 (not_1_out, A);
  not not_2 (out_13, in_9);
  not not_3 (not_3_out, C);
  not not_4 (not_4_out, B);
  not not_5 (not_5_out, D);
  not not_6 (not_6_out, A_2);
  not not_7 (not_7_out, C_2);
  not not_8 (not_8_out, B_2);
  not not_9 (not_9_out, D_2);
  not nor_1 (out_14, in_10);  // NOR_Gate
  or or_1 (or_1_out, not_1_out, D);
  or or_2 (or_2_out, not_1_out, C);
  or or_3 (or_3_out, not_1_out, not_3_out, not_4_out, not_5_out);
  nor nor_2 (nor_2_out, not_6_out, D_2);
  nor nor_3 (nor_3_out, not_6_out, C_2);
  nor nor_4 (nor_4_out, not_6_out, not_7_out, not_8_out, not_9_out);
  and and_1 (out_11, or_1_out, or_2_out, or_3_out);
  nor nor_5 (out_12, nor_2_out, nor_3_out, nor_4_out);

  // Notes on the sheet:
  //   Nick Krisulevicz
  //   EX 1
  //   Lab 7
  //   z = (A' + D)(A' + C)(A+B'+C'+D')
  //   NOR IS THE UNIVERSAL GATE
  //   POS -- NOR CONFIG
endmodule

module EX2 (
  input  A,
  input  B,
  input  C,
  input  D,
  input  A_2,
  input  B_2,
  input  C_2,
  input  D_2,
  output out_9,
  output out_10
);

  wire and_1_out, and_2_out, and_3_out, nand_1_out, nand_2_out, nand_3_out, nand_4_out, nand_5_out,
       nand_6_out, nand_7_out, not_1_out, not_2_out;

  nand nand_1 (nand_1_out, A_2, A_2, B_2);
  nand nand_2 (nand_2_out, C_2, C_2);
  nand nand_3 (nand_3_out, D_2, D_2);
  not not_1 (not_1_out, C);
  not not_2 (not_2_out, D);
  nand nand_4 (nand_4_out, nand_1_out, D_2);
  nand nand_5 (nand_5_out, A_2, D_2);
  nand nand_6 (nand_6_out, nand_2_out, nand_3_out);
  and and_1 (and_1_out, A, B, C);
  and and_2 (and_2_out, A, D);
  and and_3 (and_3_out, not_1_out, not_2_out);
  nand nand_7 (nand_7_out, nand_4_out, nand_5_out);
  or or_1 (out_9, and_1_out, and_2_out, and_3_out);
  nand nand_8 (out_10, nand_7_out, nand_6_out);

  // Notes on the sheet:
  //   EX 2
  //   Z = ABC+AD+C'D'
  //   SOP FORM -- NAND CONFIG
endmodule

module EX3 (
  input  in_1,
  input  in_2,
  input  in_3,
  input  in_4,
  input  in_5,
  input  in_6
);

  wire nand_1_out, nand_2_out, nand_3_out, nand_4_out, nand_5_out, nand_6_out, nand_7_out, nand_8_out,
       nand_9_out, nand_10_out;

  nand nand_1 (nand_1_out, in_1, in_1);
  nand nand_2 (nand_2_out, in_3, in_4);
  nand nand_3 (nand_3_out, in_5, in_6);
  nand nand_4 (nand_4_out, in_5, in_6);
  nand nand_5 (nand_5_out, in_2, in_2);
  nand nand_6 (nand_6_out, nand_2_out, nand_2_out);
  nand nand_7 (nand_7_out, nand_3_out, nand_4_out);
  nand nand_8 (nand_8_out, nand_1_out, nand_5_out);
  nand nand_9 (nand_9_out, in_4, in_4);
  nand nand_10 (nand_10_out, nand_6_out, nand_6_out, nand_9_out);

  // Notes on the sheet:
  //   EX3
  //   CONVERT CIRCUIT TO ALL NAND GATES
endmodule
