// Logisim project LAB 8.circ as structural Verilog: 3 circuits, main circuit main
module main (
  input  in_1,
  input  in_2,
  input  in_3,
  input  in_4
);

  wire n8421_converter_1_a_2, n8421_converter_1_b_2, n8421_converter_1_c_2, n8421_converter_1_d_2,
       n8421_converter_1_e, n8421_converter_1_f, n8421_converter_1_g;

  _8421_converter u_8421_converter_1 (
    .A(in_1), .B(in_2), .C(in_3), .D(in_4), .a_2(n8421_converter_1_a_2), .b_2(n8421_converter_1_b_2),
    .g(n8421_converter_1_g), .c_2(n8421_converter_1_c_2), .d_2(n8421_converter_1_d_2),
    .e(n8421_converter_1_e), .f(n8421_converter_1_f));
  _7_Segment_Display u_7_segment_display_1 (
    .g(n8421_converter_1_f), .f(n8421_converter_1_e), .a(n8421_converter_1_a_2), .b(n8421_converter_1_b_2),
    .e(n8421_converter_1_d_2), .d(n8421_converter_1_c_2), .c(n8421_converter_1_g));  // open: dp

  // Notes on the sheet:
  //   Nick Krisulevicz
  //   Lab 8
endmodule

module brainstorming (
  input  A,
  input  B,
  input  C,
  input  D,
  output a_2,
  output b_2,
  output c_2,
  output d_2,
  output e,
  output f,
  output g
);

  wire and_1_out, and_2_out, and_3_out, and_4_out, and_5_out, and_6_out, and_7_out, and_8_out, and_9_out,
       and_10_out, and_11_out, and_12_out, and_13_out, and_14_out, and_15_out, and_16_out, and_17_out,
       and_18_out, and_19_out, and_20_out, and_21_out, and_22_out, and_23_out, and_24_out, and_25_out,
       and_26_out, and_27_out, not_1_out, not_2_out, not_3_out, not_4_out, not_5_out, not_6_out, not_7_out,
       not_8_out, not_9_out, not_10_out, not_11_out, not_12_out, not_13_out, not_14_out, not_15_out,
       not_16_out, not_18_out, not_19_out, not_20_out, not_21_out, not_22_out, not_23_out, not_24_out,
       not_25_out, not_26_out, not_27_out, not_28_out, not_29_out, or_1_out, or_2_out, or_4_out, or_5_out,
       or_8_out, or_9_out, or_10_out, or_11_out, or_12_out, or_14_out, or_15_out, or_16_out, or_17_out;

  not not_1 (not_1_out, A);
  not not_2 (not_2_out, D);
  not not_3 (not_3_out, B);
  not not_4 (not_4_out, C);
  not not_5 (not_5_out, B);
  and and_1 (and_1_out, not_1_out, C, not_2_out);
  and and_2 (and_2_out, not_1_out, not_3_out, C);
  and and_3 (and_3_out, not_1_out, B, not_4_out);
  and and_4 (and_4_out, A, not_5_out, not_4_out);
  or or_1 (or_1_out, and_1_out, and_2_out);
  or or_2 (or_2_out, and_3_out, and_4_out);
  or or_3 (g, or_1_out, or_2_out);
  not not_6 (not_6_out, A);
  not not_7 (not_7_out, C);
  not not_8 (not_8_out, D);
  not not_9 (not_9_out, B);
  and and_5 (and_5_out, not_6_out, B, not_7_out);
  and and_6 (and_6_out, not_6_out, not_7_out, not_8_out);
  and and_7 (and_7_out, not_6_out, B, not_8_out);
  and and_8 (and_8_out, A, not_9_out, not_7_out);
  not not_10 (not_10_out, A);
  not not_11 (not_11_out, D);
  not not_12 (not_12_out, B);
  not not_13 (not_13_out, A);
  or or_4 (or_4_out, and_5_out, and_6_out);
  or or_5 (or_5_out, and_7_out, and_8_out);
  or or_6 (f, or_4_out, or_5_out);
  and and_9 (and_9_out, not_10_out, C, not_11_out);
  and and_10 (and_10_out, not_12_out, not_13_out, not_11_out);
  or or_7 (e, and_9_out, and_10_out);
  not not_14 (not_14_out, A);
  not not_15 (not_15_out, D);
  not not_16 (not_16_out, B);
  not not_17 (not_14_out, C);
  not not_18 (not_18_out, B);
  not not_19 (not_19_out, C);
  not not_20 (not_20_out, D);
  not not_21 (not_21_out, A);
  not not_22 (not_22_out, B);
  not not_23 (not_23_out, C);
  not not_24 (not_24_out, D);
  not not_25 (not_25_out, A);
  and and_11 (and_11_out, not_14_out, C, not_15_out);
  and and_12 (and_12_out, not_14_out, not_16_out, C);
  and and_13 (and_13_out, not_16_out, not_14_out, not_15_out);
  and and_14 (and_14_out, A, not_16_out, not_14_out, A);
  and and_15 (and_15_out, not_14_out, B, not_14_out, D);
  not not_26 (not_26_out, A);
  not not_27 (not_27_out, B);
  not not_28 (not_28_out, C);
  not not_29 (not_29_out, D);
  or or_8 (or_8_out, and_11_out, and_12_out);
  or or_9 (or_9_out, and_14_out, and_13_out);
  and and_16 (and_16_out, not_26_out, C);
  and and_17 (and_17_out, not_26_out, B, D);
  and and_18 (and_18_out, not_18_out, not_19_out, not_20_out);
  and and_19 (and_19_out, A, not_18_out, not_19_out);
  and and_20 (and_20_out, not_21_out, not_22_out);
  and and_21 (and_21_out, not_21_out, not_23_out, not_24_out);
  and and_22 (and_22_out, not_21_out, C, D);
  and and_23 (and_23_out, A, not_22_out, not_23_out);
  and and_24 (and_24_out, not_25_out, B);
  and and_25 (and_25_out, not_25_out, D, D);
  and and_26 (and_26_out, not_27_out, not_28_out, not_29_out);
  and and_27 (and_27_out, A, not_27_out, not_28_out);
  or or_10 (or_10_out, or_8_out, or_9_out);
  or or_11 (or_11_out, and_24_out, and_25_out);
  or or_12 (or_12_out, and_26_out, and_27_out);
  or or_13 (d_2, or_10_out, and_15_out);
  or or_14 (or_14_out, and_16_out, and_17_out);
  or or_15 (or_15_out, and_18_out, and_19_out);
  or or_16 (or_16_out, and_20_out, and_21_out);
  or or_17 (or_17_out, and_22_out, and_23_out);
  or or_18 (c_2, or_11_out, or_12_out);
  or or_19 (a_2, or_14_out, or_15_out);
  or or_20 (b_2, or_16_out, or_17_out);
endmodule

module _8421_converter (
  input  A,
  input  B,
  input  C,
  input  D,
  output a_2,
  output b_2,
  output g,
  output c_2,
  output d_2,
  output e,
  output f
);

  wire and_1_out, and_2_out, and_3_out, and_4_out, and_5_out, and_6_out, and_7_out, and_8_out, and_9_out,
       and_10_out, and_11_out, and_12_out, and_13_out, and_14_out, and_15_out, and_16_out, and_17_out,
       and_18_out, and_19_out, and_20_out, and_21_out, and_22_out, and_23_out, and_24_out, and_25_out,
       and_26_out, and_27_out, not_1_out, not_2_out, not_3_out, not_4_out;

  not not_1 (not_1_out, A);
  not not_2 (not_2_out, B);
  not not_3 (not_3_out, C);
  not not_4 (not_4_out, D);
  and and_1 (and_1_out, not_1_out, C);
  and and_2 (and_2_out, not_1_out, B, D);
  and and_3 (and_3_out, not_2_out, not_3_out, not_4_out);
  and and_4 (and_4_out, A, not_2_out, not_3_out);
  and and_5 (and_5_out, not_1_out, not_2_out);
  and and_6 (and_6_out, not_1_out, not_3_out, not_4_out);
  and and_7 (and_7_out, not_1_out, C, D);
  and and_8 (and_8_out, A, not_2_out, not_3_out);
  and and_9 (and_9_out, not_1_out, B);
  and and_10 (and_10_out, not_1_out, D);
  and and_11 (and_11_out, not_2_out, not_3_out, not_4_out);
  and and_12 (and_12_out, A, not_2_out, not_3_out);
  and and_13 (and_13_out, not_1_out, C, not_4_out);
  and and_14 (and_14_out, not_1_out, not_2_out, C);
  and and_15 (and_15_out, not_2_out, not_3_out, not_4_out);
  and and_16 (and_16_out, A, not_2_out, not_3_out);
  and and_17 (and_17_out, not_1_out, B, not_3_out, D);
  and and_18 (and_18_out, not_1_out, C, not_4_out);
  and and_19 (and_19_out, not_2_out, not_3_out, not_4_out);
  and and_20 (and_20_out, not_1_out, B, not_3_out);
  and and_21 (and_21_out, not_1_out, not_3_out, not_4_out);
  and and_22 (and_22_out, not_1_out, B, not_4_out);
  and and_23 (and_23_out, A, not_2_out, not_3_out);
  and and_24 (and_24_out, not_1_out, C, not_4_out);
  and and_25 (and_25_out, not_1_out, not_2_out, C);
  and and_26 (and_26_out, not_1_out, B, not_3_out);
  and and_27 (and_27_out, A, not_2_out, not_3_out);
  or or_1 (a_2, and_1_out, and_2_out, and_3_out, and_4_out);
  or or_2 (b_2, and_5_out, and_6_out, and_7_out, and_8_out);
  or or_3 (g, and_9_out, and_10_out, and_11_out, and_12_out);
  or or_4 (c_2, and_13_out, and_14_out, and_15_out, and_16_out, and_17_out);
  or or_5 (d_2, and_18_out, and_19_out);
  or or_6 (e, and_20_out, and_21_out, and_22_out, and_23_out);
  or or_7 (f, and_24_out, and_25_out, and_26_out, and_27_out);
endmodule
