// Logisim project LAB 9.circ as structural Verilog: 1 circuit, main circuit main
module main (
  input  in_1,
  input  [1:0] in_2,
  input  in_3,
  input  [2:0] in_4,
  input  [1:0] in_5,
  input  I0,
  input  I1,
  input  I2,
  input  I3,
  input  [2:0] in_10,
  input  I0_2,
  input  I1_2,
  input  I2_2,
  input  I3_2,
  input  I4,
  input  I5,
  input  I6,
  input  I7,
  input  A,
  input  B,
  output out_21,
  output out_22,
  output out_23,
  output out_24,
  output C,
  output D,
  output E
);

  wire and_1_out, and_2_out, and_3_out, and_4_out, and_5_out, and_6_out, and_7_out, and_8_out, and_9_out,
       and_10_out, and_11_out, and_12_out, decoder_1_out0, decoder_1_out1, decoder_1_out2, decoder_1_out3,
       decoder_2_out0, decoder_2_out1, decoder_2_out2, decoder_2_out3, decoder_2_out4, decoder_2_out5,
       decoder_2_out6, decoder_2_out7, not_1_out, not_2_out, not_3_out, or_2_out, or_3_out;
  wire [7:0] not_4_out;
  wire [7:1] multiplexer_2_out, undriven, undriven_2;

  not not_1 (not_1_out, in_1);
  Decoder #(.select(2)) decoder_1 (
    .out0(decoder_1_out0), .out1(decoder_1_out1), .out2(decoder_1_out2), .out3(decoder_1_out3), .sel(in_5));  // open: en
  Decoder #(.select(3)) decoder_2 (
    .out0(decoder_2_out0), .out1(decoder_2_out1), .out2(decoder_2_out2), .out3(decoder_2_out3),
    .out4(decoder_2_out4), .out5(decoder_2_out5), .out6(decoder_2_out6), .out7(decoder_2_out7), .sel(in_10));  // open: en
  not not_2 (not_2_out, A);
  not not_3 (not_3_out, B);
  Multiplexer #(.select(2)) multiplexer_1 (
    .in0(1'b0), .in1(1'b0), .in2(not_1_out), .in3(in_1), .out(out_21), .sel(in_2));  // open: en
  Multiplexer #(.select(3), .width(8)) multiplexer_2 (
    .in0({undriven, in_3}), .in1({undriven_2, 1'b1}), .in2({undriven, in_3}), .in3({undriven_2, 1'b1}),
    .in4({undriven, in_3}), .in5(not_4_out), .in6({undriven, in_3}), .in7({undriven, in_3}),
    .out({multiplexer_2_out, out_22}), .sel(in_4));  // open: en
  not not_4 (not_4_out[0], in_3);
  and and_1 (and_1_out, decoder_1_out0, I0);
  and and_2 (and_2_out, decoder_1_out1, I1);
  and and_3 (and_3_out, decoder_1_out2, I2);
  and and_4 (and_4_out, decoder_1_out3, I3);
  and and_5 (and_5_out, I0_2, decoder_2_out0);
  and and_6 (and_6_out, I1_2, decoder_2_out1);
  and and_7 (and_7_out, I2_2, decoder_2_out2);
  and and_8 (and_8_out, I3_2, decoder_2_out3);
  and and_9 (and_9_out, I4, decoder_2_out4);
  and and_10 (and_10_out, I5, decoder_2_out5);
  and and_11 (and_11_out, I6, decoder_2_out6);
  and and_12 (and_12_out, I7, decoder_2_out7);
  and and_13 (C, not_2_out, B);
  and and_14 (E, A, not_3_out);
  or or_1 (out_23, and_1_out, and_2_out, and_3_out, and_4_out);
  or or_2 (or_2_out, and_5_out, and_6_out, and_7_out, and_8_out);
  or or_3 (or_3_out, and_9_out, and_10_out, and_11_out, and_12_out);
  nor nor_1 (D, C, E);
  or or_4 (out_24, or_2_out, or_3_out);
  // Pins of 1 and 8 bits meet at {multiplexer_2_out, out_22}
  // Pins of 1 and 8 bits meet at {undriven, in_3}
  // Pins of 1 and 8 bits meet at {undriven_2, 1'b1}
  // Pins of 1 and 8 bits meet at not_4_out

  // Notes on the sheet:
  //   Nick Krisulevicz
  //   Lab 9
  //   1)
  //   2)
  //   3)
  //   4)
  //   5)
  //   MUX
  //   Decoder
  //   Comparator
  //   Check picture for completed mux circuit
  //   A<B
  //   A=B
  //   A>B
endmodule
