// Logisim project Lab 6 - Nick Krisulevicz.circ as structural Verilog: 7 circuits, main circuit main
module main (
);


  // Notes on the sheet:
  //   Lab 6
  //   Nick Krisulevicz
endmodule

module _1 (
  input  x,
  input  y,
  input  z,
  output F
);

  wire and_1_out, and_2_out, not_1_out, or_1_out, or_2_out;

  and and_1 (and_1_out, z, y, x);
  or or_1 (or_1_out, x, y);
  or or_2 (or_2_out, y, z);
  and and_2 (and_2_out, or_1_out, or_2_out);
  not not_1 (not_1_out, and_2_out);
  xor xor_1 (F, and_1_out, not_1_out);
endmodule

module _2 (
  input  d,
  input  k,
  input  s,
  input  b,
  output A
);

  wire and_1_out, and_2_out, and_3_out, not_1_out, not_2_out;

  not not_1 (not_1_out, d);
  not not_2 (not_2_out, b);
  and and_1 (and_1_out, not_1_out, k, s, b);
  and and_2 (and_2_out, not_1_out, k, s, not_2_out, not_2_out);
  and and_3 (and_3_out, d, k, s, not_2_out);
  or or_1 (A, and_1_out, k, and_2_out, and_3_out);
endmodule

module _3 (
  input  _1,
  input  _2,
  input  _3,
  input  _4,
  input  E,
  output A
);

  wire and_1_out, and_2_out, not_1_out, not_2_out;

  not not_1 (not_1_out, _2);
  not not_2 (not_2_out, _4);
  and and_1 (and_1_out, _1, not_1_out, not_2_out);
  and and_2 (and_2_out, _1, _1, _3);
  or or_1 (A, and_1_out, and_2_out, E);
endmodule

module _4 (
  input  s,
  input  d,
  input  _6,
  input  w,
  output A
);

  wire and_1_out, and_2_out, not_1_out, not_2_out;

  not not_1 (not_1_out, s);
  not not_2 (not_2_out, _6);
  and and_1 (and_1_out, not_1_out, d);
  and and_2 (and_2_out, not_2_out, w);
  or or_1 (A, and_1_out, and_2_out);
endmodule

module _5 (
  input  a,
  input  b,
  output z
);

  wire and_1_out, and_2_out, not_1_out, not_2_out;

  not not_1 (not_1_out, a);
  not not_2 (not_2_out, b);
  and and_1 (and_1_out, not_1_out, b);
  and and_2 (and_2_out, a, not_2_out);
  or or_1 (z, and_1_out, and_2_out);
endmodule

module _6 (
  input  in_1,
  input  a,
  input  in_3,
  input  b
);


  // Notes on the sheet:
  //   c
  //   d
endmodule
