// Logisim project Midterm 2 - Nick Krisulevicz.circ as structural Verilog: 2 circuits, main circuit main
module main (
  input  Stopwatch,
  input  Reset
);

  wire and_1_out, and_2_out, and_3_out, and_4_out, and_5_out, and_6_out, and_7_out, and_8_out, and_9_out,
       and_10_out, and_11_out, and_12_out, and_13_out, and_14_out, Clock_out, or_1_out, or_2_out, or_3_out,
       or_4_out, or_5_out, or_6_out, or_7_out, or_8_out, or_9_out, or_10_out, or_11_out, or_12_out,
       or_13_out, or_14_out, or_15_out, or_16_out;
  wire [3:0] counter_1_a0, counter_2_a0, counter_3_a0, counter_4_a0, counter_5_a0, counter_6_a0,
       counter_7_a0, counter_8_a0, counter_9_a0, counter_10_a0, counter_11_a0, counter_12_a0, counter_13_a0,
       counter_14_a0;

  Clock Clock (.out(Clock_out));
  or or_1 (or_1_out, Clock_out, Stopwatch);
  Hex_Digit_Display hex_digit_display_1 (.value(counter_8_a0));  // open: dp
  Hex_Digit_Display hex_digit_display_2 (.value(counter_6_a0));  // open: dp
  Hex_Digit_Display hex_digit_display_3 (.value(counter_7_a0));  // open: dp
  Hex_Digit_Display hex_digit_display_4 (.value(counter_5_a0));  // open: dp
  or or_2 (or_2_out, Reset, and_2_out, and_1_out);
  or or_3 (or_3_out, Reset, and_2_out);
  or or_4 (or_4_out, Reset, and_3_out);
  or or_5 (or_5_out, Reset, and_4_out);
  buf or_6 (or_6_out, and_5_out);  // OR_Gate
  or or_7 (or_7_out, Reset, and_6_out);
  or or_8 (or_8_out, Reset, and_7_out);
  or or_9 (or_9_out, Reset, and_8_out);
  Hex_Digit_Display hex_digit_display_5 (.value(counter_4_a0));  // open: dp
  counter counter_1 (
    .Input(and_14_out), .Reset(or_2_out), .A0(counter_1_a0[0]), .A1(counter_1_a0[1]), .A2(counter_1_a0[2]),
    .A3(counter_1_a0[3]));
  and and_1 (and_1_out, counter_1_a0[3], counter_1_a0[1]);
  counter counter_2 (
    .Input(and_1_out), .Reset(or_3_out), .A0(counter_2_a0[0]), .A1(counter_2_a0[1]), .A2(counter_2_a0[2]),
    .A3(counter_2_a0[3]));
  and and_2 (and_2_out, counter_2_a0[0], counter_2_a0[1], counter_1_a0[0]);
  counter counter_3 (
    .Input(and_2_out), .Reset(or_4_out), .A0(counter_3_a0[0]), .A1(counter_3_a0[1]), .A2(counter_3_a0[2]),
    .A3(counter_3_a0[3]));
  and and_3 (and_3_out, counter_3_a0[1], counter_3_a0[3]);
  counter counter_4 (
    .Input(and_3_out), .Reset(or_5_out), .A0(counter_4_a0[0]), .A1(counter_4_a0[1]), .A2(counter_4_a0[2]),
    .A3(counter_4_a0[3]));
  and and_4 (and_4_out, counter_4_a0[0], counter_3_a0[1], counter_3_a0[0]);
  counter counter_5 (
    .Input(and_4_out), .Reset(or_6_out), .A0(counter_5_a0[0]), .A1(counter_5_a0[1]), .A2(counter_5_a0[2]),
    .A3(counter_5_a0[3]));
  and and_5 (and_5_out, counter_5_a0[3], counter_5_a0[1]);
  counter counter_6 (
    .Input(and_5_out), .Reset(or_7_out), .A0(counter_6_a0[0]), .A1(counter_6_a0[1]), .A2(counter_6_a0[2]),
    .A3(counter_6_a0[3]));
  and and_6 (and_6_out, counter_6_a0[3], counter_6_a0[1]);
  counter counter_7 (
    .Input(and_6_out), .Reset(or_8_out), .A0(counter_7_a0[0]), .A1(counter_7_a0[1]), .A2(counter_7_a0[2]),
    .A3(counter_7_a0[3]));
  and and_7 (and_7_out, counter_7_a0[3], counter_7_a0[1]);
  counter counter_8 (
    .Input(and_7_out), .Reset(or_9_out), .A0(counter_8_a0[0]), .A1(counter_8_a0[1]), .A2(counter_8_a0[2]),
    .A3(counter_8_a0[3]));
  and and_8 (and_8_out, counter_8_a0[1], counter_8_a0[3]);
  Hex_Digit_Display hex_digit_display_6 (.value(counter_3_a0));  // open: dp
  Hex_Digit_Display hex_digit_display_7 (.value(counter_2_a0));  // open: dp
  Hex_Digit_Display hex_digit_display_8 (.value(counter_1_a0));  // open: dp
  Hex_Digit_Display hex_digit_display_9 (.value(counter_14_a0));  // open: dp
  Hex_Digit_Display hex_digit_display_10 (.value(counter_13_a0));  // open: dp
  Hex_Digit_Display hex_digit_display_11 (.value(counter_12_a0));  // open: dp
  Hex_Digit_Display hex_digit_display_12 (.value(counter_11_a0));  // open: dp
  Hex_Digit_Display hex_digit_display_13 (.value(counter_10_a0));  // open: dp
  Hex_Digit_Display hex_digit_display_14 (.value(counter_9_a0));  // open: dp
  or or_10 (or_10_out, and_13_out, and_14_out);
  or or_11 (or_11_out, Reset, and_9_out);
  or or_12 (or_12_out, Reset, and_10_out);
  or or_13 (or_13_out, Reset, and_11_out);
  or or_14 (or_14_out, Reset, and_12_out);
  or or_15 (or_15_out, Reset, or_10_out);
  or or_16 (or_16_out, Reset, and_14_out);
  counter counter_9 (
    .Input(or_1_out), .Reset(or_11_out), .A0(counter_9_a0[0]), .A1(counter_9_a0[1]), .A2(counter_9_a0[2]),
    .A3(counter_9_a0[3]));
  and and_9 (and_9_out, counter_9_a0[1], counter_9_a0[3]);
  counter counter_10 (
    .Input(and_9_out), .Reset(or_12_out), .A0(counter_10_a0[0]), .A1(counter_10_a0[1]),
    .A2(counter_10_a0[2]), .A3(counter_10_a0[3]));
  and and_10 (and_10_out, counter_10_a0[1], counter_10_a0[2]);
  counter counter_11 (
    .Input(and_10_out), .Reset(or_13_out), .A0(counter_11_a0[0]), .A1(counter_11_a0[1]),
    .A2(counter_11_a0[2]), .A3(counter_11_a0[3]));
  and and_11 (and_11_out, counter_11_a0[1], counter_11_a0[3]);
  counter counter_12 (
    .Input(and_11_out), .Reset(or_14_out), .A0(counter_12_a0[0]), .A1(counter_12_a0[1]),
    .A2(counter_12_a0[2]), .A3(counter_12_a0[3]));
  and and_12 (and_12_out, counter_12_a0[1], counter_12_a0[2]);
  counter counter_13 (
    .Input(and_12_out), .Reset(or_15_out), .A0(counter_13_a0[0]), .A1(counter_13_a0[1]),
    .A2(counter_13_a0[2]), .A3(counter_13_a0[3]));
  and and_13 (and_13_out, counter_13_a0[1], counter_13_a0[3]);
  counter counter_14 (
    .Input(and_13_out), .Reset(or_16_out), .A0(counter_14_a0[0]), .A1(counter_14_a0[1]),
    .A2(counter_14_a0[2]), .A3(counter_14_a0[3]));
  and and_14 (and_14_out, counter_14_a0[1], counter_13_a0[2]);

  // Notes on the sheet:
  //   Nick Krisulevicz
  //   Midterm II
  //   Digital Clock with Date Display and Stopwatch
  //   Year
  //   Month
  //   1st day
  //   2nd day
  //   1st month
  //   2nd month
  //   1st year
  //   2nd year
  //   3rd year
  //   4th year
  //   Day
  //   Hour
  //   Minute
  //   Second
  //   1st second
  //   2nd second
  //   1st minute
  //   2nd minute
  //   1st hour
  //   2nd hour
endmodule

module counter (
  input  Input,
  input  Reset,
  output A0,
  output A1,
  output A2,
  output A3
);

  wire d_ff_1_qn, d_ff_2_qn, d_ff_3_qn, d_ff_4_qn;

  D_Flip_Flop d_ff_1 (.clk(Input), .D(d_ff_1_qn), .Q(A0), .Qn(d_ff_1_qn), .reset(Reset));  // open: preset, en
  D_Flip_Flop d_ff_2 (.clk(d_ff_1_qn), .D(d_ff_2_qn), .Q(A1), .Qn(d_ff_2_qn), .reset(Reset));  // open: preset, en
  D_Flip_Flop d_ff_3 (.clk(d_ff_2_qn), .D(d_ff_3_qn), .Q(A2), .Qn(d_ff_3_qn), .reset(Reset));  // open: preset, en
  D_Flip_Flop d_ff_4 (.clk(d_ff_3_qn), .D(d_ff_4_qn), .Q(A3), .Qn(d_ff_4_qn), .reset(Reset));  // open: preset, en
endmodule
