// Logisim project QUIZ 2.circ as structural Verilog: 6 circuits, main circuit main
module main (
);


  // Notes on the sheet:
  //   Quiz 2
  //   11/05/2020
  //   Nick Krisulevicz
endmodule

module _1 (
  input  Ci,
  input  A,
  input  B,
  output S,
  output Ci_1
);

  wire nand_1_out, nand_2_out, nand_3_out, nand_4_out, nand_5_out, nand_6_out, nand_7_out, nand_8_out,
       nand_9_out, nand_10_out, nand_11_out, nand_12_out, nand_13_out;

  nand nand_1 (nand_1_out, A, A, B);
  nand nand_2 (nand_2_out, A, B);
  nand nand_3 (nand_3_out, A, nand_1_out);
  nand nand_4 (nand_4_out, nand_1_out, B);
  nand nand_5 (nand_5_out, nand_2_out, nand_2_out);
  nand nand_6 (nand_6_out, nand_3_out, nand_4_out);
  nand nand_7 (nand_7_out, Ci, nand_6_out);
  nand nand_8 (nand_8_out, Ci, nand_6_out);
  nand nand_9 (nand_9_out, nand_8_out, nand_8_out);
  nand nand_10 (nand_10_out, Ci, nand_7_out);
  nand nand_11 (nand_11_out, nand_7_out, nand_6_out);
  nand nand_12 (nand_12_out, nand_9_out, nand_9_out);
  nand nand_13 (nand_13_out, nand_5_out, nand_5_out);
  nand nand_14 (S, nand_10_out, nand_11_out);
  nand nand_15 (Ci_1, nand_12_out, nand_13_out);

  // Notes on the sheet:
  //   #1 full bit adder with NAND gates
endmodule

module _2 (
  input  A1,
  input  B1,
  input  A2,
  input  B2,
  output F
);

  wire and_1_out, and_2_out, and_3_out, and_4_out, D0_out, D1_out, D2_out, D3_out, not_1_out, not_2_out,
       not_3_out, not_4_out;

  not not_1 (not_1_out, B1);
  not not_2 (not_2_out, A1);
  and D0 (D0_out, not_2_out, not_1_out);
  and D1 (D1_out, not_2_out, B1);
  and D2 (D2_out, A1, not_1_out);
  and D3 (D3_out, A1, B1);
  not not_3 (not_3_out, A2);
  not not_4 (not_4_out, B2);
  and and_1 (and_1_out, D0_out, not_3_out, not_4_out);
  and and_2 (and_2_out, D1_out, not_3_out, B2);
  and and_3 (and_3_out, D2_out, not_4_out, A2);
  and and_4 (and_4_out, D3_out, A2, B2);
  or or_1 (F, and_1_out, and_2_out, and_3_out, and_4_out);

  // Notes on the sheet:
  //   4-1 MUX using decoder
endmodule

module _3 (
  input  A,
  input  B,
  input  C,
  output out_4
);

  wire and_1_out, and_2_out, and_3_out, and_4_out, and_5_out, and_6_out, and_7_out, and_8_out, and_9_out,
       and_10_out, and_11_out, not_1_out, not_2_out, not_3_out, not_4_out, not_5_out, not_6_out, not_7_out,
       not_8_out, not_9_out, or_1_out, or_2_out, or_3_out;

  not not_1 (not_1_out, A);
  not not_2 (not_2_out, A);
  not not_3 (not_3_out, A);
  and and_1 (and_1_out, not_1_out, not_2_out, not_3_out);
  and and_2 (and_2_out, not_1_out, A);
  and and_3 (and_3_out, A, not_2_out, not_3_out, A);
  and and_4 (and_4_out, A, A);
  or or_1 (or_1_out, and_4_out, and_3_out, and_2_out, and_1_out);
  not not_4 (not_4_out, A);
  not not_5 (not_5_out, A);
  not not_6 (not_6_out, A);
  and and_5 (and_5_out, not_4_out, not_5_out, not_6_out);
  and and_6 (and_6_out, not_4_out, not_5_out, A);
  and and_7 (and_7_out, not_4_out, A, not_6_out, not_4_out);
  and and_8 (and_8_out, not_4_out, A, A);
  and and_9 (and_9_out, A, not_5_out, not_6_out);
  or or_2 (or_2_out, and_9_out, and_8_out, and_7_out, and_6_out, and_5_out);
  not not_7 (not_7_out, A);
  not not_8 (not_8_out, A);
  not not_9 (not_9_out, A);
  and and_10 (and_10_out, A, A);
  and and_11 (and_11_out, not_8_out, not_9_out);
  or or_3 (or_3_out, and_11_out, and_10_out);
  or or_4 (out_4, or_3_out, or_2_out, or_1_out);

  assign B = A;
  assign C = A;

  // Notes on the sheet:
  //   Decoder for boolean function
endmodule

module _4 (
  input  C,
  input  [1:0] AB,
  output F
);

  wire not_1_out;

  not not_1 (not_1_out, C);
  Multiplexer #(.select(2)) multiplexer_1 (
    .in0(not_1_out), .in1(not_1_out), .in2(1'b0), .in3(not_1_out), .out(F), .sel(AB));  // open: en

  // Notes on the sheet:
  //   Boolen expression using MUX
endmodule

module _5 (
  input  in_1,
  input  in_2,
  input  in_3,
  output out_4,
  output out_5
);

  or or_1 (out_4, in_1, in_2);
  or or_2 (out_5, in_1, in_3);

  // Notes on the sheet:
  //   4-2 line encoder
endmodule
